# Fritzing sketch Smart_Farm_0.0.1 (saved by Fritzing 0.9.3b)
breadboards: 1

parts:
  부품1 = Arduino Mega 2560 (Rev3)
  부품3 = FC-28 Soil Hygrometer Module - Probe
  부품4 = FC-28 Soil Hygrometer Module
  MH-Real-Time_Clock_Module_3 = RTC_DS1302_module
  Grove2 = Grove Light Sensor

nets:
  N1: 부품1.A0, 부품4.AO
  N2: 부품1.A1, Grove2.SIG
  VCC: 부품1.5V, 부품4.VCC, MH-Real-Time_Clock_Module_3.VCC, Grove2.VCC
  GND: 부품1.GND, 부품4.GND, MH-Real-Time_Clock_Module_3.GND, Grove2.GND
  N3: 부품1.D2_PWM, MH-Real-Time_Clock_Module_3.RST
  N4: 부품1.D4_PWM, MH-Real-Time_Clock_Module_3.DAT
  N5: 부품1.D5_PWM, MH-Real-Time_Clock_Module_3.CLK
  N6: 부품3.POS, 부품4.POS
  N7: 부품3.NEG, 부품4.NEG

custom parts:
  FC-28 Soil Hygrometer Module - Probe: The FC-28 is a soil hygrometer module that uses the Texas Instruments LM393 comparator chip to provide an analog measurement of soil humidity.
  FC-28 Soil Hygrometer Module: The FC-28 is a soil hygrometer module that uses the Texas Instruments LM393 comparator chip to provide an analog measurement of soil humidity. The digital output is high when soil moisture is over a certain threshold, as determined by adjusting the potentiometer.
  RTC_DS1302_module: Arduino module DS1302 SPI Real Time Clock
  Grove Light Sensor: An analog light sensor
